# Fritzing sketch Circuit diagram (saved by Fritzing 0.9.1b)
stripboards: 1

parts:
  neopixel1 = Neopixel 24 Ring
  RTC1 = DS1307 RTC Breakout
  R1 = Resistor [tolerance=±1% resistance=10k package=THT]
  R2 = Resistor [tolerance=±1% resistance=10k package=THT]
  R3 = Photocell (LDR) [package=THT]
  C1 = Electrolytic Capacitor [capacitance=0.1mF voltage=6.3V package="100 mil [THT, electrolytic]"]
  U1 = attiny85 [package=dip]

nets:
  GND: neopixel1.GND, RTC1.GND, R2.Pin_0, C1.-, U1.Pin_4
  VCC: neopixel1.Vcc, RTC1.5V, R1.Pin_0, R3.pin_0, C1.+, U1.Pin_8
  N1: neopixel1.IN, U1.Pin_6
  N2: RTC1.SDA, U1.Pin_5
  N3: RTC1.SCL, U1.Pin_7
  N4: RTC1.SQW, R1.Pin_1, U1.Pin_2
  N5: R2.Pin_1, R3.pin_1, U1.Pin_3

custom parts:
  DS1307 RTC Breakout: DS1307 Real-time Clock Breakout Board with Battery
